// Logisim project T-Flip-Flop.circ as structural Verilog: 1 circuit, main circuit main
module main (
  input  T,
  input  CLK
);

  wire nand_1_out, nand_2_out, nand_3_out, nand_4_out, nand_5_out, nand_6_out, nand_7_out, nand_8_out,
       not_1_out, not_2_out, not_3_out, not_4_out, xor_1_out;

  xor xor_1 (xor_1_out, nand_7_out, T);
  not not_1 (not_1_out, CLK);
  not not_2 (not_2_out, xor_1_out);
  nand nand_1 (nand_1_out, xor_1_out, not_1_out);
  nand nand_2 (nand_2_out, not_2_out, not_1_out);
  nand nand_3 (nand_3_out, nand_1_out, nand_4_out);
  nand nand_4 (nand_4_out, nand_3_out, nand_2_out);
  not not_3 (not_3_out, not_1_out);
  not not_4 (not_4_out, nand_3_out);
  nand nand_5 (nand_5_out, nand_3_out, not_3_out);
  nand nand_6 (nand_6_out, not_4_out, not_3_out);
  nand nand_7 (nand_7_out, nand_5_out, nand_8_out);
  nand nand_8 (nand_8_out, nand_7_out, nand_6_out);
  // Probe on nand_7_out
  // Probe on nand_8_out

  // Notes on the sheet:
  //   T-Flip-Flop
  //   Казанцев Матвей Б01-406
  //   Q
  //   ~Q
endmodule
